# Fritzing sketch schema (saved by Fritzing 0.9.3b)
breadboards: 1

parts:
  DS1 = DS18B20 1-Wire Temperature Sensor [part_number=DS18B20]
  C2 = Capacitor Polarized [package=cpol-radial-100uf-25v]
  NEOPIXEL1 = Neopixel 8x8 Matrix
  U1 = NodeMCU V1.0
  R1 = Resistor [tolerance=±5% resistance=470 package="0402 [SMD]"]
  R2 = Resistor [tolerance=±5% resistance=4.7k package="0402 [SMD]"]

nets:
  GND: DS1.GND, C2.-, NEOPIXEL1.GND, U1.GND
  N1: DS1.DQ, U1.D1, R2.Pin_0
  VDD: DS1.VDD, C2.+, NEOPIXEL1.VCC, U1.3V3, R2.Pin_1
  N2: NEOPIXEL1.DIN, U1.D2, R1.Pin_0, R1.Pin_1

custom parts:
  Neopixel 8x8 Matrix: Adafruit Neopixel 8x8 Matrix
  NodeMCU V1.0: ESP8266 based NodeMCU
